# Fritzing sketch pico-joystick (saved by Fritzing 0.9.3b)

parts:
  Mod1 = Raspberry Pi Pico
  Part1 = Thumb Joystick

nets:
  N1: Mod1.pin_31, Part1.VERT
  N2: Mod1.pin_32, Part1.HORZ
  N3: Mod1.pin_36, Part1.VCC
  N4: Mod1.pin_39, Part1.GND

custom parts:
  Raspberry Pi Pico: Raspberry Pi Pico. Based around the RP2040 microcontroller the Pico is a low cost microcontroller device bringing Raspberry Pi quality, cost, and easy of use to the microcontroller space. Jan 2021, Split part in to two versions: tht (this one) and SMD. This one will drill holes for a .1 in header in pcb to allow plugging in the module as well as providing pads to solder the module to the top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
